# Fritzing sketch electronic_schematic (saved by Fritzing 0.8.7b)
breadboards: 1

parts:
  Part1 = Adafruit nRF52840 CLUE
  BATT1 = LiPoly Battery (1300mAh)
  BATT2 = LiPoly Battery (1300mAh)
  Part2 = Logic Level Converter
  U1 = TRANSISTOR_NPN_2 [package=to-92]
  J1 = Basic Servo
  U2 = Voltage Regulator - 5V [package="TO220 [THT]"]
  L1 = Solenoid

nets:
  GND: Part1.GND, BATT2.negative, Part2.GND, J1.gnd, U2.GND, L1.pin1
  N1: Part1.3.3V, Part2.LV
  N2: Part1.D2/AIN4, U1.B
  N3: Part1.D9, Part2.TX_LV
  N4: Part1.VBAT, Part2.HV, U1.C, J1.vcc, U2.output_voltage
  N5: BATT1.positive, U2.input_voltage
  N6: Part2.TX_HV, J1.pulse
  N7: U1.E, L1.pin2

custom parts:
  LiPoly Battery (1300mAh): Lithium Ion Polymer Battery (1300mAh)
